// Digital circuit SOP.dig as structural Verilog
module SOP (
  input  A,
  input  B,
  input  C,
  input  D,
  output Y
);

  wire and_1_out, and_2_out, and_3_out, and_6_out, and_7_out, not_1_out, not_2_out, not_3_out, not_4_out,
       or_1_out, or_3_out;

  not not_1 (not_1_out, A);
  not not_2 (not_2_out, B);
  not not_3 (not_3_out, C);
  not not_4 (not_4_out, D);
  and and_1 (and_1_out, not_1_out, not_2_out, D);  // open: In_4
  and and_2 (and_2_out, not_1_out, C, D);  // open: In_2
  and and_3 (and_3_out, not_1_out, not_3_out, D);  // open: In_1
  // And and_4 is placed but not wired
  // And and_5 is placed but not wired
  and and_6 (and_6_out, A, C, not_4_out);  // open: In_1
  and and_7 (and_7_out, A, not_3_out, not_4_out);  // open: In_1
  or or_1 (or_1_out, and_2_out, and_1_out);  // open: In_1, In_4
  or or_2 (Y, or_3_out, or_1_out);
  or or_3 (or_3_out, and_7_out, and_6_out, and_3_out);

  // Notes on the sheet:
  //   A: MSB
  //   D: LSB
  //   Use A as the most-significant bit and 
  //   D as the least-significant bit.
endmodule

/* Test case:
A B C D Y
0 0 0 0 X
0 0 0 1 1
*/
